// Logisim project log.circ as structural Verilog
module d_latch (
  input  in_1,
  input  in_2
);
endmodule

module d_flipflop (
);


  // Notes on the sheet:
  //   selamsssss
endmodule
